# Fritzing sketch basic_schematic - cópia (saved by Fritzing 0.9.3b)
breadboards: 1

parts:
  part = Arduino Pro Mini v13
  L1 = Inductor [package="400 mil [THT]"]
  C3 = Capacitor [part_number=470nF package=cap-pth-large]
  C2 = Capacitor [part_number=1nF package=cap-pth-small2]
  FM_Antenna = Antenna
  C1 = Capacitor [part_number=22nF package=cap-pth-large]  # not connected
  X1 = CRYSTAL [package=crystal-32khz-smd_epson_mc146]
  R3 = Resistor [tolerance=±5% resistance=2.2k package="0402 [SMD]"]
  R4 = Resistor [tolerance=±5% resistance=4.7k package="0402 [SMD]"]
  R5 = Resistor [tolerance=±5% resistance=4.7k package="0402 [SMD]"]
  C4 = Capacitor [part_number=100nF package=cap-pth-large]
  TO_AMP = Audio Jack (TRS) 3.5mm [package="4Ucon 08780 [THT]"]
  C7 = Capacitor [part_number=4.7uF package=cap-pth-large]
  C8 = Capacitor [part_number=4.7uF package=cap-pth-large]
  C5 = Capacitor [part_number=22pF package=cap-pth-large]
  C6 = Capacitor [part_number=22pF package=cap-pth-large]
  SI4735 = SSOP24 [chip_label=IC package=SSOP]  # not connected

nets:
  N1: part.A4, R4.Pin_1
  N2: part.A5, R5.Pin_0
  GND: part.GND, C4.1, C5.1, C6.1
  3.3V: part.VCC, R4.Pin_0, R5.Pin_1, C4.2
  N3: L1.pin_0, C3.2
  N4: C2.1, FM_Antenna.antenna_lead
  N5: X1.2, C6.2
  N6: X1.1, R3.Pin_0, C5.2
  N7: TO_AMP.Ring, C8.2
  N8: TO_AMP.Tip, C7.2

notes:
  SI4735 - Minimal Schematic
  Ricardo Lima Caratti - Nov 2019
  SCLK / SCL
  SDIO / SDA
  RESET (RST)
  INTERRUPT
  Left Out
  Right Out
