# Fritzing sketch basic_schematic (saved by Fritzing 0.9.3b)
circuit board: 11.6238cm x 8.48882cm
breadboards: 1

parts:
  part = Arduino Pro Mini v13
  L1 = Inductor [package="400 mil [THT]"]
  C3 = Capacitor [part_number=470nF package=cap-pth-large]
  C2 = Capacitor [part_number=1nF package=cap-pth-small2]
  FM_Antenna = Antenna
  C1 = Capacitor [part_number=22nF package=cap-pth-large]
  X1 = CRYSTAL [package=crystal-32khz-smd_epson_mc146]
  R4 = Resistor [tolerance=±5% resistance=4.7k package="0402 [SMD]"]
  R5 = Resistor [tolerance=±5% resistance=4.7k package="0402 [SMD]"]
  C4 = Capacitor [part_number=100nF package=cap-pth-large]
  TO_AMP = Audio Jack (TRS) 3.5mm [package="4Ucon 08780 [THT]"]
  C7 = Capacitor [part_number=4.7uF package=cap-pth-large]
  C8 = Capacitor [part_number=4.7uF package=cap-pth-large]
  C5 = Capacitor [part_number=22pF package=cap-pth-large]
  C6 = Capacitor [part_number=22pF package=cap-pth-large]
  part_2 = SSOP24 [chip_label=SI4735-D60 package=SSOP]
  R3 = Resistor [tolerance=±5% resistance=2.2k package="0402 [SMD]"]
  S1 = SPST Switch [package=switch-spst-smd-a]

nets (from the schematic view):
  N1: part.A4, R4.Pin_1, part_2.18
  N2: part.A5, R5.Pin_0, part_2.17
  GND: part.GND, L1.pin_1, C4.1, C5.1, C6.1, part_2.9, part_2.10, part_2.11, part_2.13, part_2.14, S1.S
  3.3V: part.VCC, R4.Pin_0, R5.Pin_1, C4.2, S1.O
  N3: part.D12/MISO, part_2.15
  N4: L1.pin_0, C3.2
  N5: C3.1, part_2.12
  N6: C2.1, FM_Antenna.antenna_lead
  N7: C2.2, part_2.8
  N8: C1.1, part_2.22
  N9: X1.2, C6.2
  N10: X1.1, C5.2, R3.Pin_0
  N11: TO_AMP.Ring, C8.2
  N12: TO_AMP.Tip, C7.2
  N13: C7.1, part_2.24
  N14: C8.1, part_2.23
  N15: part_2.3, R3.Pin_1
  N16: part_2.16, S1.P

notes:
  SI4735 - Minimal Schematic
  Ricardo Lima Caratti - Nov 2019
  SCLK / SCL
  SDIO / SDA
  RESET (RST)
  INTERRUPT
  Left Out
  Right Out
  I2C 0x11
  I2C 0x63
  I2C Addr 0x11 if SEN is connected to GND
