# Fritzing sketch basic_schematic_with_buttons_i2c (saved by Fritzing 0.9.3b)
breadboards: 1

parts:
  part = Arduino Pro Mini v13
  SI4735 = IC, DIP package, 24 pins [chip_label=IC]
  L1 = Inductor [package="400 mil [THT]"]
  C3 = Capacitor [part_number=470nF package=cap-pth-large]
  C2 = Capacitor [part_number=1nF package=cap-pth-small2]
  FM_Antenna = Antenna
  C1 = Capacitor [part_number=22nF package=cap-pth-large]
  X1 = CRYSTAL [package=crystal-32khz-smd_epson_mc146]
  R3 = Resistor [tolerance=±5% resistance=2.2k package="0402 [SMD]"]
  R4 = Resistor [tolerance=±5% resistance=10k package="0402 [SMD]"]
  R5 = Resistor [tolerance=±5% resistance=10k package="0402 [SMD]"]
  C4 = Capacitor [part_number=100nF package=cap-pth-large]
  TO_AMP = Audio Jack (TRS) 3.5mm [package="4Ucon 08780 [THT]"]
  C7 = Capacitor [part_number=4.7uF package=cap-pth-large]
  C8 = Capacitor [part_number=4.7uF package=cap-pth-large]
  C5 = Capacitor [part_number=22pF package=cap-pth-large]
  C6 = Capacitor [part_number=22pF package=cap-pth-large]
  Encoder = Rotary Encoder [package=THT]
  R6 = Resistor [tolerance=±5% resistance=10k package=THT]
  R7 = Resistor [tolerance=±5% resistance=10k package=THT]
  S1 = SWITCH-MOMENTARY-2 [package=tactile-pth-12mm]
  S2 = SWITCH-MOMENTARY-2 [package=tactile-pth-12mm]
  S3 = SWITCH-MOMENTARY-2 [package=tactile-pth-12mm]
  S4 = SWITCH-MOMENTARY-2 [package=tactile-pth-12mm]
  S5 = SWITCH-MOMENTARY-2 [package=tactile-pth-12mm]
  R8 = Resistor [tolerance=±5% resistance=10k package=THT]
  R9 = Resistor [tolerance=±5% resistance=10k package=THT]
  R10 = Resistor [tolerance=±5% resistance=10k package=THT]
  R11 = Resistor [tolerance=±5% resistance=10k package=THT]
  R12 = Resistor [tolerance=±5% resistance=10k package=THT]
  I2C_Device = OLED 128x64

nets:
  3.3V: part.VCC, part.D3_PWM, part.D2, SI4735.pin20, SI4735.pin21, R4.Pin_0, R5.Pin_1, C4.2, R7.Pin_1, S1.2, S2.2, S3.2, S4.2
  GND: part.GND, SI4735.pin10, SI4735.pin13, SI4735.pin16, C4.1, C5.1, C6.1, Encoder.EncoderPinC, R8.Pin_0, R9.Pin_0, R10.Pin_0, R11.Pin_0, R12.Pin_0, I2C_Device.GND
  N1: part.A4, SI4735.pin18, R4.Pin_1, I2C_Device.SDA
  N2: part.A5, SI4735.pin17, R5.Pin_0, I2C_Device.SCL
  N3: part.D12/MISO, SI4735.pin15
  N4: part.D9_PWM, S5.1, R12.Pin_1
  N5: part.D8, S4.1, R11.Pin_1
  N6: part.D7, S3.1, R10.Pin_1
  N7: part.D6_PWM, S2.1, R9.Pin_1
  N8: part.D5_PWM, S1.1, R8.Pin_1
  N9: SI4735.pin3, R3.Pin_1
  N10: SI4735.pin8, C2.2
  N11: SI4735.pin9, L1.pin_1
  N12: SI4735.pin12, C3.1
  N13: SI4735.pin19, X1.2, C6.2
  N14: SI4735.pin22, C1.1
  N15: SI4735.pin23, C8.1
  N16: SI4735.pin24, C7.1
  N17: L1.pin_0, C3.2
  N18: C2.1, FM_Antenna.antenna_lead
  N19: X1.1, R3.Pin_0, C5.2
  N20: TO_AMP.Ring, C8.2
  N21: TO_AMP.Tip, C7.2
  N22: Encoder.EncoderPinA, R6.Pin_0
  N23: Encoder.EncoderPinB, R7.Pin_0
  5V: S5.2
  0V: I2C_Device.VCC

notes:
  SI4735 with I2C OLED or I2C LCD 20x4
  Ricardo Lima Caratti - Nov 2019
  SLC
  SDA
  RESET (RST)
  Left Out
  Right Out
  Seek down
  seek up
  switch AM/FM
  volume up
  volume down
  Interrupt (pin 2)
  Interrupt (pin 3)
  SCL
  Look for the right display Arduino Library to control your I2C device.
  Plese, check the right voltage of your I2C device.
  3.3V or 5V

custom parts:
  OLED 128x64: Grove OLED 128x64
