# Fritzing sketch basic_schematic_with_buttons_internal_pullup_i2c (saved by Fritzing 0.9.3b)
breadboards: 1

parts:
  part = Arduino Pro Mini v13
  SI4735 = IC, DIP package, 24 pins [chip_label=IC]
  L1 = Inductor [package="400 mil [THT]"]
  C3 = Capacitor [part_number=470nF package=cap-pth-large]
  C2 = Capacitor [part_number=1nF package=cap-pth-small2]
  FM_Antenna = Antenna
  C1 = Capacitor [part_number=22nF package=cap-pth-large]
  X1 = CRYSTAL [package=crystal-32khz-smd_epson_mc146]
  R3 = Resistor [tolerance=±5% resistance=2.2k package="0402 [SMD]"]
  R4 = Resistor [tolerance=±5% resistance=10k package="0402 [SMD]"]
  R5 = Resistor [tolerance=±5% resistance=10k package="0402 [SMD]"]
  C4 = Capacitor [part_number=100nF package=cap-pth-large]
  TO_AMP = Audio Jack (TRS) 3.5mm [package="4Ucon 08780 [THT]"]
  C7 = Capacitor [part_number=4.7uF package=cap-pth-large]
  C8 = Capacitor [part_number=4.7uF package=cap-pth-large]
  C5 = Capacitor [part_number=22pF package=cap-pth-large]
  C6 = Capacitor [part_number=22pF package=cap-pth-large]
  Encoder = Rotary Encoder [package=THT]
  S1 = SWITCH-MOMENTARY-2 [package=tactile-pth-12mm]
  S2 = SWITCH-MOMENTARY-2 [package=tactile-pth-12mm]
  S3 = SWITCH-MOMENTARY-2 [package=tactile-pth-12mm]
  S4 = SWITCH-MOMENTARY-2 [package=tactile-pth-12mm]
  S5 = SWITCH-MOMENTARY-2 [package=tactile-pth-12mm]
  I2C_Device = OLED 128x64
  S6 = SWITCH-MOMENTARY-2 [package=tactile-pth]
  S7 = SWITCH-MOMENTARY-2 [package=tactile-pth]
  S8 = SWITCH-MOMENTARY-2 [package=tactile-pth]
  S9 = SWITCH-MOMENTARY-2 [package=tactile_switch_smd]

nets:
  GND: part.GND, SI4735.pin10, SI4735.pin13, SI4735.pin16, C4.1, C5.1, C6.1, Encoder.EncoderPinC, S3.1, I2C_Device.GND
  N1: part.A4, SI4735.pin18, R4.Pin_1, I2C_Device.SDA
  N2: part.A5, SI4735.pin17, R5.Pin_0, I2C_Device.SCL
  3.3V: part.VCC, SI4735.pin20, SI4735.pin21, R4.Pin_0, R5.Pin_1, C4.2
  N3: part.D13/SCK, S9.2
  N4: part.D12/MISO, SI4735.pin15
  N5: part.D11_PWM/MOSI, S8.2
  N6: part.D10_PWM/SS, S7.2
  N7: part.D9_PWM, S6.2
  N8: part.D8, S5.2
  N9: part.D7, S4.2
  N10: part.D6_PWM, S3.2
  N11: part.D5_PWM, S2.2
  N12: part.D4, S1.2
  N13: part.D3_PWM, Encoder.EncoderPinB
  N14: part.D2, Encoder.EncoderPinA
  N15: SI4735.pin3, R3.Pin_1
  N16: SI4735.pin8, C2.2
  N17: SI4735.pin9, L1.pin_1
  N18: SI4735.pin12, C3.1
  N19: SI4735.pin19, X1.2, C6.2
  N20: SI4735.pin22, C1.1
  N21: SI4735.pin23, C8.1
  N22: SI4735.pin24, C7.1
  N23: L1.pin_0, C3.2
  N24: C2.1, FM_Antenna.antenna_lead
  N25: X1.1, R3.Pin_0, C5.2
  N26: TO_AMP.Ring, C8.2
  N27: TO_AMP.Tip, C7.2
  N28: S1.1, S4.1
  0V: I2C_Device.VCC
  N29: S8.1, S9.1

notes:
  SI4735 with I2C OLED or I2C LCD 20x4
  This circuit uses Arduino internal pullup resource
  Ricardo Lima Caratti - Dec 2019
  SLC
  SDA
  RESET (RST)
  Left Out
  Right Out
  SCL
  Look for the right display Arduino Library to control your I2C device.
  Plese, check the right voltage of your I2C device.
  3.3V or 5V
  BFO
  AVC
  AVC - Automatic Volume Control ON/OFF
  BANDWIDTH - Used to select the banddwith (filter)
  AGC - Automatic Gain Control
  STEP - Used to select the increment or decrement frequency step
  BANDWIDTH
  Volume Up
  Volume Down
  Band Up
  Band Down
  AGC
  STEP

custom parts:
  OLED 128x64: Grove OLED 128x64
