# Fritzing sketch mute_circuit (saved by Fritzing 0.9.3b)
breadboards: 1

parts:
  Q1 = NPN-Transistor [part_number=2N2222 package="TO92 [THT]"]
  SI4735-D60 = SI4735-D60 [package=SSOP]
  R2 = Resistor [tolerance=±5% resistance=4.7k package=THT]
  R1 = Resistor [tolerance=±5% resistance=4.7k package=THT]
  Arduino = Arduino Pro Mini (3.3V)
  R4 = Resistor [tolerance=±5% resistance=4.7k package=THT]
  TO_AMP = Audio Jack (TRS) 3.5mm [package="4Ucon 08780 [THT]"]
  C1 = Tantalum Capacitor [capacitance=4.7µF package="100 mil [THT, tantalum]"]
  C2 = Tantalum Capacitor [capacitance=4.7µF package="100 mil [THT, tantalum]"]
  Q2 = NPN-Transistor [part_number=2N2222 package="TO92 [THT]"]
  R3 = Resistor [tolerance=±5% resistance=4.7k package=THT]

nets:
  GND: Q1.E, SI4735-D60.GND, R1.Pin_1, Arduino.GND, Q2.E, R3.Pin_1
  N1: Q1.B, R2.Pin_1
  N2: Q1.C, TO_AMP.Ring, C2.-
  N3: SI4735-D60.ROUT, C2.+
  N4: SI4735-D60.LOUT, C1.+
  N5: R2.Pin_0, Arduino.A0, R4.Pin_0
  N6: R4.Pin_1, Q2.B
  N7: TO_AMP.Tip, C1.-, Q2.C, R3.Pin_0

notes:
  D14
  A0 <=> D14
  Muting Circuit
