# Fritzing sketch ANTTENA (saved by Fritzing 0.9.3b)
breadboards: 1

parts:
  L1 = Inductor [inductance=220µH package="0603 [SMD]"]
  C1 = Ceramic Capacitor [capacitance=32pF package="100 mil [THT, multilayer]"]
  SI4735-D1 = SI4735-D60 [package=SSOP]
  U1 = TVS [package=sma-diode]
  C2 = Ceramic Capacitor [capacitance=470nF package="100 mil [THT, multilayer]"]

nets:
  N1: L1.pin_0, C1.0
  GND: L1.pin_1, U1.1
  N2: C1.1, C2.1
  N3: SI4735-D1.AMI, C2.0

notes:
  AM
